// Logisim project ALU.circ as structural Verilog
module _2_a_1_de_1_bit (
  input  ctrl,
  input  A,
  input  B,
  output Salida
);

  wire and_1_out, and_2_out;

  and and_1 (and_1_out, A, ctrl);
  and and_2 (and_2_out, ~ctrl, B);  // AND_Gate
  or or_1 (Salida, and_1_out, and_2_out);
endmodule

module _2_a_1_de_8_bits (
  input  Ctrl,
  input  [7:0] A,
  input  [7:0] B,
  output [7:0] Salida
);

  _2_a_1_de_1_bit u_2_a_1_de_1_bit_1 (.ctrl(Ctrl), .A(A[0]), .B(B[0]), .Salida(Salida[0]));
  _2_a_1_de_1_bit u_2_a_1_de_1_bit_2 (.ctrl(Ctrl), .A(A[1]), .B(B[1]), .Salida(Salida[1]));
  _2_a_1_de_1_bit u_2_a_1_de_1_bit_3 (.ctrl(Ctrl), .A(A[2]), .B(B[2]), .Salida(Salida[2]));
  _2_a_1_de_1_bit u_2_a_1_de_1_bit_4 (.ctrl(Ctrl), .A(A[3]), .B(B[3]), .Salida(Salida[3]));
  _2_a_1_de_1_bit u_2_a_1_de_1_bit_5 (.ctrl(Ctrl), .A(A[4]), .B(B[4]), .Salida(Salida[4]));
  _2_a_1_de_1_bit u_2_a_1_de_1_bit_6 (.ctrl(Ctrl), .A(A[5]), .B(B[5]), .Salida(Salida[5]));
  _2_a_1_de_1_bit u_2_a_1_de_1_bit_7 (.ctrl(Ctrl), .A(A[6]), .B(B[6]), .Salida(Salida[6]));
  _2_a_1_de_1_bit u_2_a_1_de_1_bit_8 (.ctrl(Ctrl), .A(A[7]), .B(B[7]), .Salida(Salida[7]));
endmodule

module _8_a_1_de_8_bits (
  input  [2:0] Ctrl,
  input  [7:0] e7,
  input  [7:0] e6,
  input  [7:0] e5,
  input  [7:0] e4,
  input  [7:0] e3,
  input  [7:0] e2,
  input  [7:0] e1,
  input  [7:0] e0,
  output [7:0] out_10
);

  wire [7:0] n2_a_1_de_8_bits_1_salida, n2_a_1_de_8_bits_2_salida, n2_a_1_de_8_bits_3_salida,
       n2_a_1_de_8_bits_4_salida, n2_a_1_de_8_bits_5_salida, n2_a_1_de_8_bits_6_salida;

  _2_a_1_de_8_bits u_2_a_1_de_8_bits_1 (.A(e7), .B(e6), .Ctrl(Ctrl[0]), .Salida(n2_a_1_de_8_bits_1_salida));
  _2_a_1_de_8_bits u_2_a_1_de_8_bits_2 (.A(e5), .B(e4), .Ctrl(Ctrl[0]), .Salida(n2_a_1_de_8_bits_2_salida));
  _2_a_1_de_8_bits u_2_a_1_de_8_bits_3 (.A(e3), .B(e2), .Ctrl(Ctrl[0]), .Salida(n2_a_1_de_8_bits_3_salida));
  _2_a_1_de_8_bits u_2_a_1_de_8_bits_4 (.A(e1), .B(e0), .Ctrl(Ctrl[0]), .Salida(n2_a_1_de_8_bits_4_salida));
  _2_a_1_de_8_bits u_2_a_1_de_8_bits_5 (
    .A(n2_a_1_de_8_bits_1_salida), .B(n2_a_1_de_8_bits_2_salida), .Ctrl(Ctrl[1]),
    .Salida(n2_a_1_de_8_bits_5_salida));
  _2_a_1_de_8_bits u_2_a_1_de_8_bits_6 (
    .A(n2_a_1_de_8_bits_3_salida), .B(n2_a_1_de_8_bits_4_salida), .Ctrl(Ctrl[1]),
    .Salida(n2_a_1_de_8_bits_6_salida));
  _2_a_1_de_8_bits u_2_a_1_de_8_bits_7 (
    .A(n2_a_1_de_8_bits_5_salida), .B(n2_a_1_de_8_bits_6_salida), .Ctrl(Ctrl[2]), .Salida(out_10));
endmodule

module FA (
  input  A,
  input  B,
  input  Carry,
  output Salida,
  output Carry_2
);

  wire and_1_out, and_2_out, and_3_out, and_4_out, and_5_out, and_6_out, and_7_out;

  and and_1 (and_1_out, A, ~Carry_2);  // AND_Gate
  and and_2 (and_2_out, B, ~Carry_2);  // AND_Gate
  and and_3 (and_3_out, Carry, ~Carry_2);  // AND_Gate
  and and_4 (and_4_out, A, B, Carry);
  and and_5 (and_5_out, A, B);
  and and_6 (and_6_out, A, Carry);
  and and_7 (and_7_out, B, Carry);
  or or_1 (Salida, and_1_out, and_2_out, and_3_out, and_4_out);
  or or_2 (Carry_2, and_5_out, and_6_out, and_7_out);
endmodule

// 1
module FA_8_bits (
  input  _1er_carry,
  input  [7:0] A,
  input  [7:0] B,
  output [7:0] Salida,
  output Carry
);

  wire fa_1_carry_2, fa_2_carry_2, fa_3_carry_2, fa_4_carry_2, fa_5_carry_2, fa_6_carry_2, fa_7_carry_2;

  FA fa_1 (.A(A[0]), .B(B[0]), .Carry(_1er_carry), .Salida(Salida[0]), .Carry_2(fa_1_carry_2));
  FA fa_2 (.A(A[1]), .B(B[1]), .Carry(fa_1_carry_2), .Salida(Salida[1]), .Carry_2(fa_2_carry_2));
  FA fa_3 (.A(A[2]), .B(B[2]), .Carry(fa_2_carry_2), .Salida(Salida[2]), .Carry_2(fa_3_carry_2));
  FA fa_4 (.A(A[3]), .B(B[3]), .Carry(fa_3_carry_2), .Salida(Salida[3]), .Carry_2(fa_4_carry_2));
  FA fa_5 (.A(A[4]), .B(B[4]), .Carry(fa_4_carry_2), .Salida(Salida[4]), .Carry_2(fa_5_carry_2));
  FA fa_6 (.A(A[5]), .B(B[5]), .Carry(fa_5_carry_2), .Salida(Salida[5]), .Carry_2(fa_6_carry_2));
  FA fa_7 (.A(A[6]), .B(B[6]), .Carry(fa_6_carry_2), .Salida(Salida[6]), .Carry_2(fa_7_carry_2));
  FA fa_8 (.A(A[7]), .B(B[7]), .Carry(fa_7_carry_2), .Salida(Salida[7]), .Carry_2(Carry));
endmodule

module Negador (
  input  A,
  input  Cntrol,
  output out_3
);

  xor xor_1 (out_3, A, Cntrol);
endmodule

module Negador_8_bits (
  input  [7:0] Entrada,
  input  Control,
  output [7:0] Salida
);

  Negador negador_1 (.A(Entrada[0]), .Cntrol(Control), .out_3(Salida[0]));
  Negador negador_2 (.A(Entrada[1]), .Cntrol(Control), .out_3(Salida[1]));
  Negador negador_3 (.A(Entrada[2]), .Cntrol(Control), .out_3(Salida[2]));
  Negador negador_4 (.A(Entrada[3]), .Cntrol(Control), .out_3(Salida[3]));
  Negador negador_5 (.A(Entrada[4]), .Cntrol(Control), .out_3(Salida[4]));
  Negador negador_6 (.A(Entrada[5]), .Cntrol(Control), .out_3(Salida[5]));
  Negador negador_7 (.A(Entrada[6]), .Cntrol(Control), .out_3(Salida[6]));
  Negador negador_8 (.A(Entrada[7]), .Cntrol(Control), .out_3(Salida[7]));
endmodule

module circuit (
  input  [7:0] A,
  input  [7:0] B,
  input  Ctrl,
  output [7:0] Salida,
  output out_5
);

  wire [7:0] negador_8_bits_1_salida;

  Negador_8_bits negador_8_bits_1 (.Entrada(B), .Control(Ctrl), .Salida(negador_8_bits_1_salida));
  FA_8_bits fa_8_bits_1 (._1er_carry(Ctrl), .A(A), .B(negador_8_bits_1_salida), .Carry(out_5), .Salida(Salida));
endmodule

module a__1 (
  input  [7:0] Entrada,
  output [7:0] Salida
);


  assign Salida = {1'b0, Entrada[7:1]};
  // also tied to GND on the sheet: Entrada[0]
endmodule

// A<<1
module a__1_2 (
  input  [7:0] Entrada,
  output [7:0] out_2
);


  assign out_2 = {Entrada[6:0], 1'b0};
  // also tied to GND on the sheet: Entrada[7]
endmodule

// and
module AND (
  input  [7:0] A,
  input  [7:0] B,
  output [7:0] Salida
);

  assign Salida = A & B;  // AND_Gate and_1, 8 bits wide
endmodule

// or
module OR (
  input  [7:0] A,
  input  [7:0] B,
  output [7:0] Salida
);

  assign Salida = A | B;  // OR_Gate or_1, 8 bits wide
endmodule

// xor
module XOR (
  input  [7:0] A,
  input  [7:0] B,
  output [7:0] Salida
);

  assign Salida = A ^ B;  // XOR_Gate xor_1, 8 bits wide
endmodule

module ALU (
  input  [2:0] Ctrl,
  input  [7:0] A,
  input  [7:0] B,
  output [7:0] Salida
);

  wire [7:0] a_1_1_salida, a_1_2_out_2, and_1_salida, or_1_salida, part_1_salida, xor_1_salida;

  a__1 a_1_1 (.Entrada(A), .Salida(a_1_1_salida));
  XOR xor_1 (.A(A), .B(B), .Salida(xor_1_salida));
  OR or_1 (.A(A), .B(B), .Salida(or_1_salida));
  AND and_1 (.A(A), .B(B), .Salida(and_1_salida));
  circuit part_1 (.A(A), .B(B), .Ctrl(Ctrl[0]), .Salida(part_1_salida));  // open: out_5
  a__1_2 a_1_2 (.Entrada(A), .out_2(a_1_2_out_2));
  Multiplexor multiplexor_1 (
    .e7(a_1_1_salida), .e6(xor_1_salida), .e5(or_1_salida), .e4(and_1_salida), .e3(part_1_salida),
    .e2(part_1_salida), .e1(a_1_2_out_2), .e0(A), .Ctrl_0(Ctrl[0]), .Ctrl_1(Ctrl[1]), .Ctrl_2(Ctrl[2]),
    .Salida(Salida));
endmodule
