// Logisim project Banco de registros.circ as structural Verilog
module Latch_D (
  input  D,
  input  En,
  input  Ra,
  output out_4,
  output out_5
);

  wire and_1_out, and_2_out, nor_1_out, nor_2_out;

  and and_1 (and_1_out, D, En);
  and and_2 (and_2_out, En, ~D);  // AND_Gate
  nor nor_1 (nor_1_out, and_1_out, out_5);
  buf buffer_1 (out_4, nor_1_out);
  nor nor_2 (nor_2_out, out_4, and_2_out);
  or or_1 (out_5, nor_2_out, Ra);
endmodule

module Flip_flop (
  input  In,
  input  Ra,
  input  Clk,
  output Q,
  output nQ
);

  wire latch_d_1_out_4, latch_d_1_out_5, not_1_out;

  not not_1 (not_1_out, Clk);
  Latch_D latch_d_1 (.D(In), .En(not_1_out), .Ra(Ra), .out_4(latch_d_1_out_4), .out_5(latch_d_1_out_5));
  Latch_D latch_d_2 (.D(latch_d_1_out_4), .En(Clk), .Ra(Ra), .out_4(Q), .out_5(nQ));
endmodule

module Register (
  input  [7:0] Entrada,
  input  Ra,
  input  Enable,
  output [7:0] Salida
);

  wire and_1_out, Clk_out;

  Flip_flop flip_flop_1 (.In(Entrada[0]), .Ra(Ra), .Clk(and_1_out), .Q(Salida[0]));  // open: nQ
  Flip_flop flip_flop_2 (.In(Entrada[1]), .Ra(Ra), .Clk(and_1_out), .Q(Salida[1]));  // open: nQ
  Flip_flop flip_flop_3 (.In(Entrada[2]), .Ra(Ra), .Clk(and_1_out), .Q(Salida[2]));  // open: nQ
  Flip_flop flip_flop_4 (.In(Entrada[3]), .Ra(Ra), .Clk(and_1_out), .Q(Salida[3]));  // open: nQ
  Flip_flop flip_flop_5 (.In(Entrada[4]), .Ra(Ra), .Clk(and_1_out), .Q(Salida[4]));  // open: nQ
  Flip_flop flip_flop_6 (.In(Entrada[5]), .Ra(Ra), .Clk(and_1_out), .Q(Salida[5]));  // open: nQ
  Flip_flop flip_flop_7 (.In(Entrada[6]), .Ra(Ra), .Clk(and_1_out), .Q(Salida[6]));  // open: nQ
  Flip_flop flip_flop_8 (.In(Entrada[7]), .Ra(Ra), .Clk(and_1_out), .Q(Salida[7]));  // open: nQ
  and and_1 (and_1_out, Clk_out, Enable);
  Clock Clk (.out(Clk_out));
endmodule

module Register_Bank (
  input  [7:0] Entrada,
  input  We,
  input  [3:0] Rd,
  input  [3:0] Rs,
  input  Clk,
  input  Reset,
  output [7:0] Salida
);

  wire demultiplexer_1_out0, demultiplexer_1_out1, demultiplexer_1_out2, demultiplexer_1_out3,
       demultiplexer_1_out4, demultiplexer_1_out5, demultiplexer_1_out6, demultiplexer_1_out7,
       demultiplexer_1_out8, demultiplexer_1_out9, demultiplexer_1_out10, demultiplexer_1_out11,
       demultiplexer_1_out12, demultiplexer_1_out13, demultiplexer_1_out14, demultiplexer_1_out15;
  wire [7:0] register_1_q, register_2_q, register_3_q, register_4_q, register_5_q, register_6_q,
       register_7_q, register_8_q, register_9_q, register_10_q, register_11_q, register_12_q, register_13_q,
       register_14_q, register_15_q, register_16_q;

  Demultiplexer #(.select(4)) demultiplexer_1 (
    .out0(demultiplexer_1_out0), .out1(demultiplexer_1_out1), .out2(demultiplexer_1_out2),
    .out3(demultiplexer_1_out3), .out4(demultiplexer_1_out4), .out5(demultiplexer_1_out5),
    .out6(demultiplexer_1_out6), .out7(demultiplexer_1_out7), .out8(demultiplexer_1_out8),
    .out9(demultiplexer_1_out9), .out10(demultiplexer_1_out10), .out11(demultiplexer_1_out11),
    .out12(demultiplexer_1_out12), .out13(demultiplexer_1_out13), .out14(demultiplexer_1_out14),
    .out15(demultiplexer_1_out15), .in(We), .sel(Rd), .en(1'b1));
  Register_part register_1 (.D(Entrada), .en(demultiplexer_1_out0), .Q(register_1_q), .clk(Clk), .clr(Reset));
  Register_part register_2 (.D(Entrada), .en(demultiplexer_1_out1), .Q(register_2_q), .clk(Clk), .clr(Reset));
  Register_part register_3 (.D(Entrada), .en(demultiplexer_1_out2), .Q(register_3_q), .clk(Clk), .clr(Reset));
  Register_part register_4 (.D(Entrada), .en(demultiplexer_1_out3), .Q(register_4_q), .clk(Clk), .clr(Reset));
  Register_part register_5 (.D(Entrada), .en(demultiplexer_1_out4), .Q(register_5_q), .clk(Clk), .clr(Reset));
  Register_part register_6 (.D(Entrada), .en(demultiplexer_1_out5), .Q(register_6_q), .clk(Clk), .clr(Reset));
  Register_part register_7 (.D(Entrada), .en(demultiplexer_1_out6), .Q(register_7_q), .clk(Clk), .clr(Reset));
  Register_part register_8 (.D(Entrada), .en(demultiplexer_1_out7), .Q(register_8_q), .clk(Clk), .clr(Reset));
  Register_part register_9 (.D(Entrada), .en(demultiplexer_1_out8), .Q(register_9_q), .clk(Clk), .clr(Reset));
  Register_part register_10 (.D(Entrada), .en(demultiplexer_1_out9), .Q(register_10_q), .clk(Clk), .clr(Reset));
  Register_part register_11 (.D(Entrada), .en(demultiplexer_1_out10), .Q(register_11_q), .clk(Clk), .clr(Reset));
  Register_part register_12 (.D(Entrada), .en(demultiplexer_1_out11), .Q(register_12_q), .clk(Clk), .clr(Reset));
  Register_part register_13 (.D(Entrada), .en(demultiplexer_1_out12), .Q(register_13_q), .clk(Clk), .clr(Reset));
  Register_part register_14 (.D(Entrada), .en(demultiplexer_1_out13), .Q(register_14_q), .clk(Clk), .clr(Reset));
  Register_part register_15 (.D(Entrada), .en(demultiplexer_1_out14), .Q(register_15_q), .clk(Clk), .clr(Reset));
  Register_part register_16 (.D(Entrada), .en(demultiplexer_1_out15), .Q(register_16_q), .clk(Clk), .clr(Reset));
  Multiplexer #(.select(4), .width(8)) multiplexer_1 (
    .in0(register_1_q), .in1(register_2_q), .in2(register_3_q), .in3(register_4_q), .in4(register_5_q),
    .in5(register_6_q), .in6(register_7_q), .in7(register_8_q), .in8(register_9_q), .in9(register_10_q),
    .in10(register_11_q), .in11(register_12_q), .in12(register_13_q), .in13(register_14_q),
    .in14(register_15_q), .in15(register_16_q), .out(Salida), .sel(Rs), .en(1'b1));
endmodule
