// Logisim project DU.circ as structural Verilog: 1 circuit, main circuit main
module main (
  input  [7:0] Entrada,
  output in_en,
  output reg_en,
  output [2:0] OP,
  output regA_we,
  output out_we,
  output reg_we,
  output imm_en
);

  wire and_1_out, and_2_out, and_3_out, and_4_out, and_5_out, and_6_out, and_7_out, and_8_out, and_9_out,
       and_10_out, and_11_out, and_12_out, and_13_out, and_14_out, and_15_out, and_16_out, and_17_out,
       and_18_out, and_19_out, and_20_out, and_21_out, and_22_out, and_23_out, and_24_out, and_25_out,
       and_26_out, and_27_out, and_28_out, and_29_out, and_30_out, and_31_out, and_32_out, and_33_out,
       and_34_out, and_35_out, and_36_out, and_37_out, and_38_out, and_39_out, and_40_out, and_41_out,
       and_42_out, and_43_out, and_44_out, and_45_out, and_46_out, and_47_out, and_48_out, and_49_out,
       and_50_out, and_51_out, and_52_out, and_53_out, and_54_out, and_55_out, and_56_out, and_57_out,
       and_58_out, and_60_out, and_61_out, and_62_out, and_63_out, and_64_out, and_65_out, and_66_out,
       and_67_out, and_68_out, and_69_out, and_70_out, and_71_out, and_72_out, and_73_out, and_76_out,
       and_77_out, and_78_out, and_79_out, and_81_out, and_82_out, not_1_out, not_2_out, not_3_out,
       not_4_out, not_5_out, not_6_out, not_7_out, not_8_out, not_9_out, not_10_out, not_11_out, not_12_out,
       not_13_out, not_14_out, not_15_out, not_16_out, not_17_out, not_18_out, not_19_out, not_20_out,
       not_21_out, not_22_out, not_23_out, not_24_out, not_25_out, not_26_out, not_27_out, not_28_out,
       not_29_out, not_30_out, not_31_out, not_32_out, not_33_out, not_34_out, not_35_out, not_36_out,
       not_37_out, not_38_out, not_39_out, not_40_out, not_41_out, not_42_out, not_43_out, not_44_out,
       not_45_out, not_46_out, not_47_out, not_48_out, not_49_out, not_50_out, not_51_out, not_52_out,
       not_53_out, not_54_out, not_55_out, not_56_out, not_57_out, not_58_out, not_59_out, not_60_out,
       not_61_out, not_62_out, not_63_out, not_64_out, not_65_out, not_66_out, not_67_out, not_68_out,
       not_69_out, not_70_out, not_71_out, not_72_out, not_73_out, not_74_out, not_75_out, not_76_out,
       or_1_out, or_2_out, or_3_out, or_4_out, or_6_out, or_7_out;

  not not_1 (not_1_out, Entrada[5]);
  and and_1 (and_1_out, not_1_out, not_2_out);
  not not_2 (not_2_out, Entrada[4]);
  not not_3 (not_3_out, Entrada[3]);
  not not_4 (not_4_out, Entrada[2]);
  and and_2 (and_2_out, not_4_out, not_5_out);
  not not_5 (not_5_out, Entrada[1]);
  not not_6 (not_6_out, Entrada[5]);
  not not_7 (not_7_out, Entrada[3]);
  not not_8 (not_8_out, Entrada[2]);
  not not_9 (not_9_out, Entrada[5]);
  and and_3 (and_3_out, not_9_out, not_10_out);
  not not_10 (not_10_out, Entrada[3]);
  not not_11 (not_11_out, Entrada[1]);
  not not_12 (not_12_out, Entrada[0]);
  not not_13 (not_13_out, Entrada[5]);
  not not_14 (not_14_out, Entrada[3]);
  not not_15 (not_15_out, Entrada[2]);
  and and_4 (and_4_out, Entrada[5], not_16_out);
  not not_16 (not_16_out, Entrada[4]);
  not not_17 (not_17_out, Entrada[3]);
  not not_18 (not_18_out, Entrada[2]);
  not not_19 (not_19_out, Entrada[1]);
  not not_20 (not_20_out, Entrada[5]);
  and and_5 (and_5_out, not_20_out, Entrada[4]);
  not not_21 (not_21_out, Entrada[3]);
  not not_22 (not_22_out, Entrada[2]);
  not not_23 (not_23_out, Entrada[5]);
  and and_6 (and_6_out, not_23_out, Entrada[4]);
  not not_24 (not_24_out, Entrada[3]);
  and and_7 (and_7_out, Entrada[2], not_25_out);
  not not_25 (not_25_out, Entrada[1]);
  not not_26 (not_26_out, Entrada[0]);
  not not_27 (not_27_out, Entrada[4]);
  not not_28 (not_28_out, Entrada[2]);
  not not_29 (not_29_out, Entrada[1]);
  not not_30 (not_30_out, Entrada[5]);
  and and_8 (and_8_out, not_30_out, Entrada[4]);
  not not_31 (not_31_out, Entrada[3]);
  not not_32 (not_32_out, Entrada[2]);
  not not_33 (not_33_out, Entrada[1]);
  not not_34 (not_34_out, Entrada[5]);
  and and_9 (and_9_out, not_34_out, Entrada[4]);
  not not_35 (not_35_out, Entrada[3]);
  not not_36 (not_36_out, Entrada[1]);
  not not_37 (not_37_out, Entrada[0]);
  not not_38 (not_38_out, Entrada[4]);
  not not_39 (not_39_out, Entrada[2]);
  not not_40 (not_40_out, Entrada[1]);
  not not_41 (not_41_out, Entrada[5]);
  and and_10 (and_10_out, not_41_out, Entrada[4]);
  not not_42 (not_42_out, Entrada[3]);
  not not_43 (not_43_out, Entrada[2]);
  and and_11 (and_11_out, Entrada[5], not_44_out);
  not not_44 (not_44_out, Entrada[4]);
  not not_45 (not_45_out, Entrada[3]);
  not not_46 (not_46_out, Entrada[2]);
  not not_47 (not_47_out, Entrada[1]);
  not not_48 (not_48_out, Entrada[5]);
  and and_12 (and_12_out, not_48_out, not_49_out);
  not not_49 (not_49_out, Entrada[4]);
  not not_50 (not_50_out, Entrada[3]);
  not not_51 (not_51_out, Entrada[1]);
  not not_52 (not_52_out, Entrada[5]);
  and and_13 (and_13_out, not_52_out, not_53_out);
  not not_53 (not_53_out, Entrada[4]);
  not not_54 (not_54_out, Entrada[3]);
  not not_55 (not_55_out, Entrada[2]);
  and and_14 (and_14_out, not_55_out, Entrada[1]);
  not not_56 (not_56_out, Entrada[0]);
  not not_57 (not_57_out, Entrada[5]);
  not not_58 (not_58_out, Entrada[3]);
  not not_59 (not_59_out, Entrada[2]);
  not not_60 (not_60_out, Entrada[5]);
  not not_61 (not_61_out, Entrada[3]);
  not not_62 (not_62_out, Entrada[2]);
  not not_63 (not_63_out, Entrada[5]);
  and and_15 (and_15_out, not_63_out, Entrada[4]);
  not not_64 (not_64_out, Entrada[3]);
  not not_65 (not_65_out, Entrada[1]);
  not not_66 (not_66_out, Entrada[0]);
  and and_16 (and_16_out, Entrada[5], not_67_out);
  not not_67 (not_67_out, Entrada[4]);
  not not_68 (not_68_out, Entrada[3]);
  not not_69 (not_69_out, Entrada[2]);
  not not_70 (not_70_out, Entrada[1]);
  not not_71 (not_71_out, Entrada[5]);
  and and_17 (and_17_out, not_71_out, not_72_out);
  not not_72 (not_72_out, Entrada[4]);
  not not_73 (not_73_out, Entrada[3]);
  and and_18 (and_18_out, Entrada[2], not_74_out);
  not not_74 (not_74_out, Entrada[1]);
  and and_19 (and_19_out, and_1_out, not_3_out);
  and and_20 (and_20_out, and_2_out, Entrada[0]);
  and and_21 (and_21_out, not_6_out, not_7_out);
  and and_22 (and_22_out, not_8_out, Entrada[1]);
  and and_23 (and_23_out, and_3_out, Entrada[2]);
  and and_24 (and_24_out, not_11_out, not_12_out);
  and and_25 (and_25_out, not_13_out, Entrada[4]);
  and and_26 (and_26_out, not_14_out, not_15_out);
  and and_27 (and_27_out, and_4_out, not_17_out);
  and and_28 (and_28_out, not_18_out, not_19_out);
  and and_29 (and_29_out, and_5_out, not_21_out);
  and and_30 (and_30_out, not_22_out, Entrada[1]);
  and and_31 (and_31_out, and_6_out, not_24_out);
  and and_32 (and_32_out, and_7_out, not_26_out);
  and and_33 (and_33_out, Entrada[5], not_27_out);
  not not_75 (not_75_out, Entrada[3]);
  and and_34 (and_34_out, not_28_out, not_29_out);
  and and_35 (and_35_out, and_8_out, not_31_out);
  and and_36 (and_36_out, not_32_out, not_33_out);
  and and_37 (and_37_out, and_9_out, not_35_out);
  and and_38 (and_38_out, not_36_out, not_37_out);
  and and_39 (and_39_out, Entrada[5], not_38_out);
  not not_76 (not_76_out, Entrada[3]);
  and and_40 (and_40_out, not_39_out, not_40_out);
  and and_41 (and_41_out, and_10_out, not_42_out);
  and and_42 (and_42_out, not_43_out, Entrada[0]);
  and and_43 (and_43_out, and_11_out, not_45_out);
  and and_44 (and_44_out, not_46_out, not_47_out);
  and and_45 (and_45_out, and_12_out, not_50_out);
  and and_46 (and_46_out, Entrada[2], not_51_out);
  and and_47 (and_47_out, and_13_out, not_54_out);
  and and_48 (and_48_out, and_14_out, not_56_out);
  and and_49 (and_49_out, not_57_out, not_58_out);
  and and_50 (and_50_out, not_59_out, Entrada[0]);
  and and_51 (and_51_out, not_60_out, Entrada[4]);
  and and_52 (and_52_out, not_61_out, not_62_out);
  and and_53 (and_53_out, and_15_out, not_64_out);
  and and_54 (and_54_out, not_65_out, not_66_out);
  and and_55 (and_55_out, and_16_out, not_68_out);
  and and_56 (and_56_out, not_69_out, not_70_out);
  and and_57 (and_57_out, and_17_out, not_73_out);
  and and_58 (and_58_out, and_18_out, Entrada[0]);
  and and_59 (in_en, and_19_out, and_20_out);
  and and_60 (and_60_out, and_21_out, and_22_out);
  and and_61 (and_61_out, and_23_out, and_24_out);
  and and_62 (and_62_out, and_25_out, and_26_out);
  and and_63 (and_63_out, and_27_out, and_28_out);
  and and_64 (and_64_out, and_29_out, and_30_out);
  and and_65 (and_65_out, and_31_out, and_32_out);
  and and_66 (and_66_out, and_33_out, not_75_out);
  and and_67 (and_67_out, and_34_out, Entrada[0]);
  and and_68 (and_68_out, and_35_out, and_36_out);
  and and_69 (and_69_out, and_37_out, and_38_out);
  and and_70 (and_70_out, and_39_out, not_76_out);
  and and_71 (and_71_out, and_40_out, Entrada[0]);
  and and_72 (and_72_out, and_41_out, and_42_out);
  and and_73 (and_73_out, and_43_out, and_44_out);
  and and_74 (regA_we, and_45_out, and_46_out);
  and and_75 (out_we, and_47_out, and_48_out);
  and and_76 (and_76_out, and_49_out, and_50_out);
  and and_77 (and_77_out, and_51_out, and_52_out);
  and and_78 (and_78_out, and_53_out, and_54_out);
  and and_79 (and_79_out, and_55_out, and_56_out);
  and and_80 (imm_en, and_57_out, and_58_out);
  or or_1 (or_1_out, and_60_out, and_61_out);
  or or_2 (or_2_out, and_62_out, and_63_out);
  or or_3 (or_3_out, and_64_out, and_65_out);
  and and_81 (and_81_out, and_66_out, and_67_out);
  or or_4 (or_4_out, and_68_out, and_69_out);
  and and_82 (and_82_out, and_70_out, and_71_out);
  or or_5 (OP[0], and_72_out, and_73_out);
  or or_6 (or_6_out, and_76_out, and_77_out);
  or or_7 (or_7_out, and_78_out, and_79_out);
  or or_8 (reg_en, or_1_out, or_2_out);
  or or_9 (OP[2], or_3_out, and_81_out);
  or or_10 (OP[1], or_4_out, and_82_out);
  or or_11 (reg_we, or_6_out, or_7_out);
endmodule
