// Logisim project Mux.circ as structural Verilog: 4 circuits, main circuit main
module main (
  input  in_1,
  input  in_2,
  input  in_3,
  output out_4
);

  and and_1 (out_4, in_1, in_2, in_3);
endmodule

module Multiplexor (
  input  Ctrl_0,
  input  Ctrl_1,
  input  Ctrl_2,
  input  [7:0] e7,
  input  [7:0] e6,
  input  [7:0] e5,
  input  [7:0] e4,
  input  [7:0] e3,
  input  [7:0] e2,
  input  [7:0] e1,
  input  [7:0] e0,
  output [7:0] Salida
);

  wire [7:0] n2_a_1_de_8_bits_1_salida, n2_a_1_de_8_bits_2_salida, n2_a_1_de_8_bits_3_salida,
       n2_a_1_de_8_bits_4_salida, n2_a_1_de_8_bits_5_salida, n2_a_1_de_8_bits_6_salida;

  _2_a_1_de_8_bits u_2_a_1_de_8_bits_1 (.A(e7), .B(e6), .Ctrl(Ctrl_0), .Salida(n2_a_1_de_8_bits_1_salida));
  _2_a_1_de_8_bits u_2_a_1_de_8_bits_2 (.A(e5), .B(e4), .Ctrl(Ctrl_0), .Salida(n2_a_1_de_8_bits_2_salida));
  _2_a_1_de_8_bits u_2_a_1_de_8_bits_3 (.A(e3), .B(e2), .Ctrl(Ctrl_0), .Salida(n2_a_1_de_8_bits_3_salida));
  _2_a_1_de_8_bits u_2_a_1_de_8_bits_4 (.A(e1), .B(e0), .Ctrl(Ctrl_0), .Salida(n2_a_1_de_8_bits_4_salida));
  _2_a_1_de_8_bits u_2_a_1_de_8_bits_5 (
    .A(n2_a_1_de_8_bits_1_salida), .B(n2_a_1_de_8_bits_2_salida), .Ctrl(Ctrl_1),
    .Salida(n2_a_1_de_8_bits_5_salida));
  _2_a_1_de_8_bits u_2_a_1_de_8_bits_6 (
    .A(n2_a_1_de_8_bits_3_salida), .B(n2_a_1_de_8_bits_4_salida), .Ctrl(Ctrl_1),
    .Salida(n2_a_1_de_8_bits_6_salida));
  _2_a_1_de_8_bits u_2_a_1_de_8_bits_7 (
    .A(n2_a_1_de_8_bits_5_salida), .B(n2_a_1_de_8_bits_6_salida), .Ctrl(Ctrl_2), .Salida(Salida));
endmodule

module _2_a_1_de_1_bit (
  input  ctrl,
  input  A,
  input  B,
  output Salida
);

  wire and_1_out, and_2_out;

  and and_1 (and_1_out, A, ctrl);
  and and_2 (and_2_out, ~ctrl, B);  // AND_Gate
  or or_1 (Salida, and_1_out, and_2_out);
endmodule

module _2_a_1_de_8_bits (
  input  Ctrl,
  input  [7:0] A,
  input  [7:0] B,
  output [7:0] Salida
);

  _2_a_1_de_1_bit u_2_a_1_de_1_bit_1 (.ctrl(Ctrl), .A(A[0]), .B(B[0]), .Salida(Salida[0]));
  _2_a_1_de_1_bit u_2_a_1_de_1_bit_2 (.ctrl(Ctrl), .A(A[1]), .B(B[1]), .Salida(Salida[1]));
  _2_a_1_de_1_bit u_2_a_1_de_1_bit_3 (.ctrl(Ctrl), .A(A[2]), .B(B[2]), .Salida(Salida[2]));
  _2_a_1_de_1_bit u_2_a_1_de_1_bit_4 (.ctrl(Ctrl), .A(A[3]), .B(B[3]), .Salida(Salida[3]));
  _2_a_1_de_1_bit u_2_a_1_de_1_bit_5 (.ctrl(Ctrl), .A(A[4]), .B(B[4]), .Salida(Salida[4]));
  _2_a_1_de_1_bit u_2_a_1_de_1_bit_6 (.ctrl(Ctrl), .A(A[5]), .B(B[5]), .Salida(Salida[5]));
  _2_a_1_de_1_bit u_2_a_1_de_1_bit_7 (.ctrl(Ctrl), .A(A[6]), .B(B[6]), .Salida(Salida[6]));
  _2_a_1_de_1_bit u_2_a_1_de_1_bit_8 (.ctrl(Ctrl), .A(A[7]), .B(B[7]), .Salida(Salida[7]));
endmodule
