// Logisim project Procesador.circ as structural Verilog
module Procesador (
  input  [7:0] Input,
  input  Reset,
  output [2:0] out_3,
  output [7:0] Salida_Register,
  output [7:0] SalidaALU,
  output [7:0] Salida
);

  wire Clk_out, DU_imm_en, DU_in_en, DU_out_we, DU_reg_en, DU_reg_we, DU_rega_we;
  wire [7:0] BR_salida, controlled_buffer_1_out;
  wire [15:0] IR_q, ROM_out_3;

  Clock Clk (.out(Clk_out));
  assign controlled_buffer_1_out = DU_in_en ? Input : 8'bz;  // Controlled_Buffer controlled_buffer_1
  Register #(.width(16)) IR (.D(ROM_out_3), .Q(IR_q), .clk(Clk_out));  // open: en, clr
  assign controlled_buffer_1_out = DU_imm_en ? IR_q[7:0] : 8'bz;  // Controlled_Buffer controlled_buffer_2
  Register RegOut (.D(SalidaALU), .en(DU_out_we), .Q(Salida), .clk(Clk_out), .clr(Reset));
  Register_Bank BR (
    .Entrada(SalidaALU), .We(DU_reg_we), .Rd(IR_q[3:0]), .Clk(Clk_out), .Salida(BR_salida), .Rs(IR_q[7:4]),
    .Reset(Reset));
  DU_main DU (
    .Entrada(IR_q[15:8]), .in_en(DU_in_en), .reg_en(DU_reg_en), .OP(out_3), .regA_we(DU_rega_we),
    .out_we(DU_out_we), .reg_we(DU_reg_we), .imm_en(DU_imm_en));
  assign controlled_buffer_1_out = DU_reg_en ? BR_salida : 8'bz;  // Controlled_Buffer controlled_buffer_3
  ROM ROM (.Reset(Reset), .out_3(ROM_out_3), .Clk(Clk_out));
  Register RegA (.D(controlled_buffer_1_out), .en(DU_rega_we), .Q(Salida_Register), .clk(Clk_out), .clr(Reset));
  ALU ALU (.Ctrl(out_3), .A(controlled_buffer_1_out), .B(Salida_Register), .Salida(SalidaALU));
endmodule
