// Logisim project Rom Counter.circ as structural Verilog
module Program_Counter (
  input  Clock,
  input  Reset,
  output [7:0] Salida
);

  wire and_1_out, and_2_out, and_3_out, and_4_out, and_5_out, and_6_out, d_ff_1_qn, xor_1_out, xor_2_out,
       xor_3_out, xor_4_out, xor_5_out, xor_6_out, xor_7_out;

  D_Flip_Flop d_ff_1 (
    .clk(Clock), .D(d_ff_1_qn), .Q(Salida[0]), .Qn(d_ff_1_qn), .en(1'b1), .reset(Reset));  // open: preset
  xor xor_1 (xor_1_out, Salida[0], Salida[1]);
  D_Flip_Flop d_ff_2 (.clk(Clock), .D(xor_1_out), .Q(Salida[1]), .en(1'b1), .reset(Reset));  // open: Qn, preset
  and and_1 (and_1_out, Salida[1], Salida[0]);
  xor xor_2 (xor_2_out, and_1_out, Salida[2]);
  D_Flip_Flop d_ff_3 (.clk(Clock), .D(xor_2_out), .Q(Salida[2]), .en(1'b1), .reset(Reset));  // open: Qn, preset
  and and_2 (and_2_out, Salida[2], and_1_out, Salida[0]);
  xor xor_3 (xor_3_out, and_2_out, Salida[3]);
  D_Flip_Flop d_ff_4 (.clk(Clock), .D(xor_3_out), .Q(Salida[3]), .en(1'b1), .reset(Reset));  // open: Qn, preset
  and and_3 (and_3_out, Salida[3], and_2_out, and_1_out, Salida[0]);
  xor xor_4 (xor_4_out, and_3_out, Salida[4]);
  D_Flip_Flop d_ff_5 (.clk(Clock), .D(xor_4_out), .Q(Salida[4]), .en(1'b1), .reset(Reset));  // open: Qn, preset
  and and_4 (and_4_out, Salida[4], and_3_out, and_2_out, and_1_out, Salida[0]);
  xor xor_5 (xor_5_out, and_4_out, Salida[5]);
  D_Flip_Flop d_ff_6 (.clk(Clock), .D(xor_5_out), .Q(Salida[5]), .en(1'b1), .reset(Reset));  // open: Qn, preset
  and and_5 (and_5_out, Salida[5], and_4_out, and_3_out, and_2_out, and_1_out, Salida[0]);
  D_Flip_Flop d_ff_7 (.clk(Clock), .D(xor_6_out), .Q(Salida[6]), .en(1'b1), .reset(Reset));  // open: Qn, preset
  xor xor_6 (xor_6_out, and_5_out, Salida[6]);
  and and_6 (and_6_out, Salida[6], and_5_out, and_4_out, and_3_out, and_2_out, and_1_out, Salida[0]);
  xor xor_7 (xor_7_out, and_6_out, Salida[7]);
  D_Flip_Flop d_ff_8 (.clk(Clock), .D(xor_7_out), .Q(Salida[7]), .en(1'b1), .reset(Reset));  // open: Qn, preset
endmodule

module ROM (
  input  Clk,
  input  Reset,
  output [15:0] out_3
);

  wire [7:0] program_counter_1_salida;

  Program_Counter program_counter_1 (.Clock(Clk), .Reset(Reset), .Salida(program_counter_1_salida));
  ROM_part #(.dataWidth(16)) rom_1 (.addr(program_counter_1_salida), .data(out_3));  // open: sel
  Program_Counter program_counter_2 ();  // open: Clock, Reset, Salida

  // Notes on the sheet:
  //   contents of rom_1 (hex, n*v repeats v):
  //   103 430 1034 1145 1346 1207 34e 230 240 250 260 270 2080 2d0 2e0
endmodule
