// Logisim project registro.circ as structural Verilog
module Latch_D (
  input  D,
  input  En,
  input  RA,
  output Q,
  output Q_2
);

  wire and_1_out, and_2_out, nor_1_out, nor_2_out;

  and and_1 (and_1_out, D, En);
  and and_2 (and_2_out, En, ~D);  // AND_Gate
  nor nor_1 (nor_1_out, and_1_out, Q_2);
  nor nor_2 (nor_2_out, Q, and_2_out);
  buf buffer_1 (Q, nor_1_out);
  or or_1 (Q_2, nor_2_out, RA);
endmodule

module Flip_Flop_D (
  input  D,
  input  in_2,
  input  Clock,
  output Q,
  output Q_2
);

  wire latch_d_1_q, not_1_out;

  not not_1 (not_1_out, Clock);
  Latch_D latch_d_1 (.D(D), .En(not_1_out), .RA(in_2), .Q(latch_d_1_q));  // open: Q_2
  Latch_D latch_d_2 (.D(latch_d_1_q), .En(Clock), .RA(in_2), .Q(Q), .Q_2(Q_2));
endmodule

module Registro (
  input  [7:0] Entrada,
  input  Reset,
  input  Enable,
  output [7:0] Salida
);

  wire and_1_out, Clock_out;

  Clock Clock (.out(Clock_out));
  Flip_Flop_D flip_flop_d_1 (.D(Entrada[0]), .in_2(Reset), .Clock(and_1_out), .Q(Salida[0]));  // open: Q_2
  Flip_Flop_D flip_flop_d_2 (.D(Entrada[1]), .in_2(Reset), .Clock(and_1_out), .Q(Salida[1]));  // open: Q_2
  Flip_Flop_D flip_flop_d_3 (.D(Entrada[2]), .in_2(Reset), .Clock(and_1_out), .Q(Salida[2]));  // open: Q_2
  Flip_Flop_D flip_flop_d_4 (.D(Entrada[3]), .in_2(Reset), .Clock(and_1_out), .Q(Salida[3]));  // open: Q_2
  Flip_Flop_D flip_flop_d_5 (.D(Entrada[4]), .in_2(Reset), .Clock(and_1_out), .Q(Salida[4]));  // open: Q_2
  Flip_Flop_D flip_flop_d_6 (.D(Entrada[5]), .in_2(Reset), .Clock(and_1_out), .Q(Salida[5]));  // open: Q_2
  Flip_Flop_D flip_flop_d_7 (.D(Entrada[6]), .in_2(Reset), .Clock(and_1_out), .Q(Salida[6]));  // open: Q_2
  Flip_Flop_D flip_flop_d_8 (.D(Entrada[7]), .in_2(Reset), .Clock(and_1_out), .Q(Salida[7]));  // open: Q_2
  and and_1 (and_1_out, Clock_out, Enable);
endmodule

module Banco_de_Registros (
  input  [7:0] IN,
  input  WE,
  input  [3:0] RD,
  input  [3:0] RS,
  input  Reset,
  output [7:0] out_6
);

  wire Clock_out, demultiplexer_1_out0, demultiplexer_1_out1, demultiplexer_1_out2, demultiplexer_1_out3,
       demultiplexer_1_out4, demultiplexer_1_out5, demultiplexer_1_out6, demultiplexer_1_out7,
       demultiplexer_1_out8, demultiplexer_1_out9, demultiplexer_1_out10, demultiplexer_1_out11,
       demultiplexer_1_out12, demultiplexer_1_out13, demultiplexer_1_out14, demultiplexer_1_out15;
  wire [7:0] register_1_q, register_2_q, register_3_q, register_4_q, register_5_q, register_6_q,
       register_7_q, register_8_q, register_9_q, register_10_q, register_11_q, register_12_q, register_13_q,
       register_14_q, register_15_q, register_16_q;

  Demultiplexer #(.select(4)) demultiplexer_1 (
    .out0(demultiplexer_1_out0), .out1(demultiplexer_1_out1), .out2(demultiplexer_1_out2),
    .out3(demultiplexer_1_out3), .out4(demultiplexer_1_out4), .out5(demultiplexer_1_out5),
    .out6(demultiplexer_1_out6), .out7(demultiplexer_1_out7), .out8(demultiplexer_1_out8),
    .out9(demultiplexer_1_out9), .out10(demultiplexer_1_out10), .out11(demultiplexer_1_out11),
    .out12(demultiplexer_1_out12), .out13(demultiplexer_1_out13), .out14(demultiplexer_1_out14),
    .out15(demultiplexer_1_out15), .in(WE), .sel(RD), .en(1'b1));
  Register register_1 (.D(IN), .en(demultiplexer_1_out0), .Q(register_1_q), .clk(Clock_out), .clr(Reset));
  Register register_2 (.D(IN), .en(demultiplexer_1_out1), .Q(register_2_q), .clk(Clock_out), .clr(Reset));
  Register register_3 (.D(IN), .en(demultiplexer_1_out2), .Q(register_3_q), .clk(Clock_out), .clr(Reset));
  Register register_4 (.D(IN), .en(demultiplexer_1_out3), .Q(register_4_q), .clk(Clock_out), .clr(Reset));
  Register register_5 (.D(IN), .en(demultiplexer_1_out4), .Q(register_5_q), .clk(Clock_out), .clr(Reset));
  Register register_6 (.D(IN), .en(demultiplexer_1_out5), .Q(register_6_q), .clk(Clock_out), .clr(Reset));
  Register register_7 (.D(IN), .en(demultiplexer_1_out6), .Q(register_7_q), .clk(Clock_out), .clr(Reset));
  Register register_8 (.D(IN), .en(demultiplexer_1_out7), .Q(register_8_q), .clk(Clock_out), .clr(Reset));
  Register register_9 (.D(IN), .en(demultiplexer_1_out8), .Q(register_9_q), .clk(Clock_out), .clr(Reset));
  Register register_10 (.D(IN), .en(demultiplexer_1_out9), .Q(register_10_q), .clk(Clock_out), .clr(Reset));
  Register register_11 (.D(IN), .en(demultiplexer_1_out10), .Q(register_11_q), .clk(Clock_out), .clr(Reset));
  Register register_12 (.D(IN), .en(demultiplexer_1_out11), .Q(register_12_q), .clk(Clock_out), .clr(Reset));
  Register register_13 (.D(IN), .en(demultiplexer_1_out12), .Q(register_13_q), .clk(Clock_out), .clr(Reset));
  Register register_14 (.D(IN), .en(demultiplexer_1_out13), .Q(register_14_q), .clk(Clock_out), .clr(Reset));
  Register register_15 (.D(IN), .en(demultiplexer_1_out14), .Q(register_15_q), .clk(Clock_out), .clr(Reset));
  Register register_16 (.D(IN), .en(demultiplexer_1_out15), .Q(register_16_q), .clk(Clock_out), .clr(Reset));
  Clock Clock (.out(Clock_out));
  Multiplexer #(.select(4), .width(8)) multiplexer_1 (
    .in0(register_1_q), .in1(register_2_q), .in2(register_3_q), .in3(register_4_q), .in4(register_5_q),
    .in5(register_6_q), .in6(register_7_q), .in7(register_8_q), .in8(register_9_q), .in9(register_10_q),
    .in10(register_11_q), .in11(register_12_q), .in12(register_13_q), .in13(register_14_q),
    .in14(register_15_q), .in15(register_16_q), .out(out_6), .sel(RS), .en(1'b1));
endmodule
